# Fritzing sketch 16x (saved by Fritzing 0.9.3b)

parts:
  Part2 = 16-Channel 12-bit PWM Servo Driver - I2C [part_number=815]
  Part3 = Arduino Nano (Rev3.0)
  JACK2 = 2.1mm Barrel Jack with Terminal Block
  C2 = Electrolytic Capacitor [capacitance=1000µF package="300 mil [THT, electrolytic]"]
  Part4 = 16-Channel 12-bit PWM Servo Driver - I2C [part_number=815]
  JACK3 = 2.1mm Barrel Jack with Terminal Block
  C3 = Electrolytic Capacitor [capacitance=1000µF package="300 mil [THT, electrolytic]"]

nets:
  N1: Part2.5.0V, C2.+
  GND: Part2.GND, Part3.GND, JACK2.NEG, C2.-, Part4.GND, JACK3.NEG, C3.-
  N2: Part2.PWRIN, JACK2.POS
  VCC: Part2.VCC, Part3.5V, Part4.VCC
  N3: Part2.SDA, Part3.A4, Part4.SDA
  N4: Part2.SCL, Part3.A5, Part4.SCL
  N5: Part4.5.0V, C3.+
  N6: Part4.PWRIN, JACK3.POS

custom parts:
  16-Channel 12-bit PWM Servo Driver - I2C: You want to make a cool robot, maybe a hexapod walker, or maybe just a piece of art with a lot of moving parts. Or maybe you want to drive a lot of LEDs with precise PWM output. Using only two pins, control 16 free-running PWM outputs! You can even chain up 62 breakouts to control up to 992 PWM outputs.
